# Fritzing sketch circuit (saved by Fritzing 0.9.3b)
breadboards: 1

parts:
  U1 = ESP8266 WiFi Module [part_number=ESP8266]
  S3 = Toggle Switch [package=THT]
  RESET = Pushbutton [package="[THT]"]
  U2 = Voltage Regulator - 3.3V [package="TO220 [THT]"]
  C1 = Electrolytic Capacitor [capacitance=100µF package="200 mil [THT, electrolytic]"]
  J1 = female pin header, 2 pins [form="♀ (female)"]
  Part1 = Arduino Pro Mini (3.3V)
  R1 = Temperature Sensor (Thermistor) [thermistor_type=NTC package=THT]
  R2 = Resistor [tolerance=±5% resistance=10k package="2512 [SMD]"]
  Part2 = Adafruit Si7021 Temp Humidity [part_number="Adafruit #3251"]
  R3 = Temperature Sensor (Thermistor) [thermistor_type=NTC package=THT]
  R4 = Resistor [tolerance=±5% resistance=10k package="2512 [SMD]"]

nets:
  N1: U1.RXD, J1.pin1
  VCC: U1.VCC, U1.GPIO_2, U1.CH_PD, U2.output_voltage, C1.+, Part1.VCC, Part2.+3V3
  N2: U1.GPIO_0, S3.COM
  GND: U1.GND, U1.GPIO_15, U1.GPIO_16, U1.REST, S3.L1, RESET.Pin_1, RESET.Pin_2, RESET.Pin_3, RESET.Pin_4, U2.GND, C1.-, Part1.GND, R1.pin_1, Part2.GND, R3.pin_0
  N3: U1.TXD, J1.pin2
  N4: U1.GPIO_4, Part1.A4, Part2.SDA
  N5: U1.GPIO_5, Part1.A5, Part2.SCL
  N6: U1.GPIO_12, Part1.RESET
  N7: Part1.A1, R1.pin_0, R2.Pin_1
  N8: Part1.A0, R3.pin_1, R4.Pin_1
  N9: Part1.D7, R2.Pin_0, R4.Pin_0

custom parts:
  Adafruit Si7021 Temp Humidity: It's summer and you're sweating and your hair's all frizzy and all you really want to know is why the weatherman said this morning that today's relative humidity would max out at a perfectly reasonable 42% when it feels more like 77%. Enter the Si7021 Temperature + Humidity Sensor - the best way to prove the weatherman wrong! This lovely sensor for Silicon labs has ± 3% relative humidity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
